// Logisim project Quartz_version_0.circ as structural Verilog: 1 circuit, main circuit main
module main (
);

  wire and_1_out, and_2_out, C_CIR_LATCH, C_CLOCK, C_IDX_ENABLE, C_IDX_LATCH, C_MAR_LATCH, C_MDR_ENABLE,
       C_MDR_LATCH, C_MEM_READ, C_MEM_WRITE, C_PC_ENABLE, C_PC_LATCH, C_RESET, not_1_out, not_2_out, or_1_out;
  wire [7:0] controlled_buffer_4_out, controlled_buffer_6_out, controlled_buffer_8_out, MDR_q, ram_1_dout,
       rom_1_data;
  wire [15:0] controlled_buffer_1_out, IDX_q, MAR_q, PC_q;
  wire [15:12] pull_resistor_1_node;

  // Probe on C_CLOCK
  // Probe on C_PC_LATCH
  // Probe on C_PC_ENABLE
  // Probe on C_MAR_LATCH
  // Probe on C_MEM_WRITE
  // Probe on C_RESET
  // Probe on C_MEM_READ
  // Probe on C_MDR_ENABLE
  // Probe on C_MDR_LATCH
  // Probe on C_IDX_LATCH
  // Probe on C_IDX_ENABLE
  // Probe on C_CIR_LATCH
  // Probe on pull_resistor_1_node[12]
  // Probe on pull_resistor_1_node[13]
  // Probe on pull_resistor_1_node[14]
  // Probe on pull_resistor_1_node[15]
  Pull_Resistor pull_resistor_1 (.node({pull_resistor_1_node, C_CIR_LATCH, C_IDX_ENABLE, C_IDX_LATCH, C_MDR_LATCH, C_MDR_ENABLE, C_MEM_READ, C_RESET, C_MEM_WRITE, C_MAR_LATCH, C_PC_ENABLE, C_PC_LATCH, C_CLOCK}));
  // Switch switch_1: pin names not known; wires that end beside it: C_CLOCK
  // Switch switch_2: pin names not known; wires that end beside it: C_PC_LATCH
  // Switch switch_3: pin names not known; wires that end beside it: C_PC_ENABLE
  // Switch switch_4: pin names not known; wires that end beside it: C_MAR_LATCH
  // Switch switch_5: pin names not known; wires that end beside it: C_MEM_WRITE
  // Switch switch_6: pin names not known; wires that end beside it: C_RESET
  // Switch switch_7: pin names not known; wires that end beside it: C_MEM_READ
  // Switch switch_8: pin names not known; wires that end beside it: C_MDR_ENABLE
  // Switch switch_9: pin names not known; wires that end beside it: C_MDR_LATCH
  // Switch switch_10: pin names not known; wires that end beside it: C_IDX_LATCH
  // Switch switch_11: pin names not known; wires that end beside it: C_IDX_ENABLE
  // Switch switch_12: pin names not known; wires that end beside it: C_CIR_LATCH
  // Switch switch_13: pin names not known; wires that end beside it: pull_resistor_1_node[12], pull_resistor_1_node[12]
  // Switch switch_14: pin names not known; wires that end beside it: pull_resistor_1_node[13], pull_resistor_1_node[13]
  // Switch switch_15: pin names not known; wires that end beside it: pull_resistor_1_node[14], pull_resistor_1_node[14]
  // Switch switch_16: pin names not known; wires that end beside it: pull_resistor_1_node[15], pull_resistor_1_node[15], 1'b1
  Register #(.width(16)) PC (.D(controlled_buffer_1_out), .en(C_PC_LATCH), .clk(C_CLOCK), .Q(PC_q), .clr(C_RESET));
  assign controlled_buffer_1_out = C_PC_ENABLE ? PC_q : 16'bz;  // Controlled_Buffer controlled_buffer_1
  Pull_Resistor pull_resistor_2 (.node(controlled_buffer_1_out));
  // Probe on controlled_buffer_1_out
  Register #(.width(16)) MAR (.D(controlled_buffer_1_out), .en(C_MAR_LATCH), .clk(C_CLOCK), .Q(MAR_q), .clr(C_RESET));
  Register #(.width(16)) IDX (.D(controlled_buffer_1_out), .en(C_IDX_LATCH), .clk(C_CLOCK), .Q(IDX_q), .clr(C_RESET));
  ROM #(.addrWidth(15)) rom_1 (.addr(MAR_q[14:0]), .data(rom_1_data));
  RAM #(.addrWidth(15)) ram_1 (
    .addr(MAR_q[14:0]), .we(C_MEM_WRITE), .oe(not_1_out), .clk(C_CLOCK), .din(controlled_buffer_6_out),
    .dout(ram_1_dout));
  not not_1 (not_1_out, C_MEM_WRITE);
  assign controlled_buffer_1_out[7:0] = C_IDX_ENABLE ? IDX_q[7:0] : 8'bz;  // Controlled_Buffer controlled_buffer_2
  assign controlled_buffer_1_out[15:8] = C_IDX_ENABLE ? IDX_q[15:8] : 8'bz;  // Controlled_Buffer controlled_buffer_3
  not not_2 (not_2_out, MAR_q[15]);
  and and_1 (and_1_out, C_MEM_READ, not_2_out);
  and and_2 (and_2_out, MAR_q[15], C_MEM_READ);
  assign controlled_buffer_4_out = and_1_out ? rom_1_data : 8'bz;  // Controlled_Buffer controlled_buffer_4
  assign controlled_buffer_4_out = and_2_out ? ram_1_dout : 8'bz;  // Controlled_Buffer controlled_buffer_5
  assign controlled_buffer_6_out = C_MEM_WRITE ? MDR_q : 8'bz;  // Controlled_Buffer controlled_buffer_6
  assign controlled_buffer_4_out = C_MDR_LATCH ? controlled_buffer_8_out : 8'bz;  // Controlled_Buffer controlled_buffer_7
  or or_1 (or_1_out, C_MDR_LATCH, C_MEM_READ);
  Register MDR (.D(controlled_buffer_4_out), .en(or_1_out), .clk(C_CLOCK), .Q(MDR_q), .clr(C_RESET));
  assign controlled_buffer_8_out = C_MDR_ENABLE ? MDR_q : 8'bz;  // Controlled_Buffer controlled_buffer_8
  Pull_Resistor pull_resistor_3 (.node(controlled_buffer_8_out));
  // Probe on controlled_buffer_8_out
  Register CIR (.D(controlled_buffer_8_out), .en(C_CIR_LATCH), .clk(C_CLOCK), .clr(C_RESET));  // open: Q

  // Notes on the sheet:
  //   contents of rom_1 (hex, n*v repeats v):
  //   de ad
endmodule
